# Fritzing sketch Parade Locomotive Player v5 (saved by Fritzing 0.9.10b)
perfboards: 3

parts:
  PCF8574_IO_Expansion = pcf8574 io expansion board [package=THT]
  Generic_4x4_button_keypad1 = Generic 4x4 Keypad  # not connected
  DY-SV5W = sv5w
  S3 = Taiway 100-SP-X-T1 SPDT Miniature Toggle Switch [part_number=100-SP-X-T1-0-0-B1-M2 package=THT]
  LCD2 = LCD screen  # not connected
  Part2 = Arduino Nano (Rev3.0) (ICSP)
  SP3 = SPEAKER [package=pcb_mount_speaker]  # not connected
  SP4 = SPEAKER [package=pcb_mount_speaker]  # not connected
  M1 = RioRand LM2596
  F2 = FUSE [package=fuse_5mm]
  F3 = FUSE [package=fuse_5mm]
  F5 = FUSE [package=fuse_5mm]  # not connected
  J3 = Screw terminal - 2 pins [package=THT]
  F4 = FUSE [package=fuse_5mm]
  BAT2 = Battery Holders [package=battery]
  S5 = Round Pushbutton
  PCF8574_IO_Expansion1 = pcf8574 io expansion board [package=THT]
  U2 = POT [knob_status=75% power=0.5W package=pot_mammoth]  # not connected

nets:
  N1: PCF8574_IO_Expansion.SDA, Part2.A4, PCF8574_IO_Expansion1.SDA
  N2: PCF8574_IO_Expansion.SCL, Part2.A5, PCF8574_IO_Expansion1.SCL
  N3: PCF8574_IO_Expansion.A2c, PCF8574_IO_Expansion.A2-
  N4: DY-SV5W.TXD/IO0, Part2.D1/TX
  N5: DY-SV5W.RXD/IO1, DY-SV5W.IO2, Part2.D0/RX
  N6: S3.COM, BAT2.+
  N7: S3.L1, J3.pin1
  N8: Part2.VIN, M1.Pin_3
  N9: Part2.RESET, S5.leg0
  N10: M1.Pin_1, F4.2
  N11: M1.Pin_2, F4.1
  N12: F2.1, F3.1
  N13: J3.pin2, BAT2.-

notes:
  LCD Backlight
  Power
  Kenwood KDC-895
  Yellow - 12V Constant Power
  Red - 12 V Switched Power
  White - Left Front Speaker +
  Grey - Right Front Speaker +
  Green - Left Rear Speaker +
  Violet - Right Rear Speaker +
  Orange/White - Illumination
  Blue - Power Antenna
  Black - Chassis Ground
  White/Black - Left Front Sp -
  Grey/Black - Right Front Sp -
  Green/Black - Left Rear Sp -
  Vilot/Black - Right Rear Sp -
  Cab Panel
  Engine Compartment
  D4 D5 D6 D7 A  K
  Right Fender Speaker
  Left Fender Speaker
  Barrel Jack to To KDC-895 Aux Input
  15-12 vdc -> 9 buck converter
  KDC-895 Head Unit Harness
  Fuse Block
  1) Fender Speakers: Rockville RWB65W:
  Peak Power Handling : 500 Watts (250 Watts/Speaker)
  RMS Power Handling : 300 Watts (150 Watts/Speaker)
  Frequency Response : 70 – 20,000 Hz
  Sound Pressure Level : 96dB @ 1w/1m
  Impedance : 4 Ohms )
  Not Used Yet
  1. Motorola TDN6253A Siren Speaker 11 Ohm 100 Watts
  with 70 Amp Alternator
  12 Volt Car Battery
  Reset
  40et8 Voiture 410 Parade Train Player Version 1.0
  Chisled, Built, and Coded by Paul Ciarelli   ©Three Paul Productions, 2023
  Donated to Voiture 410 by Linda & Paul Ciarelli

custom parts:
  pcf8574 io expansion board: pcf8574 io expansion board.
  Generic 4x4 Keypad: generic 4x4 keypad 4 rows of four 6 mm tact switches cheap and nasty but works
  sv5w: DY-SV5W is an intelligent voice module. It integrates I/O subsection triggering, UART serial port control, ONE_line single bus serial port control3. Onboard 5W Class D amplifier circuit and can directly drive 4ohm 3~5W speakers. Support MP3,WAV decoding format. Max support 32Gbit(4MByte) TF card memory, can connect the computer to update TF card to store audio files via USB cable.
